// Logisim project MIPS.circ as structural Verilog: 2 circuits, main circuit main
module main (
);

  wire and_1_out, buff_20_1_out_2, CLK, comparator_1_eq, controlunit_1_out_3, controlunit_1_out_4,
       controlunit_1_out_5, controlunit_1_out_6, controlunit_1_out_7, controlunit_1_out_8,
       controlunit_1_out_9, hazard_unit_1_flushe, hazard_unit_1_forwardad, hazard_unit_1_forwardbd,
       hazard_unit_1_stalld, hazard_unit_1_stallf, reg_stage2_1_alusrce, reg_stage2_1_memtorege,
       reg_stage2_1_memwritee, reg_stage2_1_regdste, reg_stage2_1_regwritee, reg_stage3_1_p8,
       reg_stage3_1_p9, reg_stage3_1_p10, reg_stage4_1_memtoregw, reg_stage4_1_regwritew;
  wire [1:0] hazard_unit_1_forwardae, hazard_unit_1_forwardbe;
  wire [3:0] adder_1_out_2, controlunit_1_out_10, reg_stage2_1_aluctrle;
  wire [4:0] multiplexer_5_out, reg_stage2_1_rde, reg_stage2_1_rse, reg_stage2_1_rte, reg_stage3_1_p13,
       reg_stage4_1_writeregw;
  wire [27:0] adder_1_out, bit_extender_1_out, shifter_1_out;
  wire [31:0] adder_2_out, bit_extender_2_out, datamem_1_rd, instmem_1_out_2, multiplexer_1_out,
       multiplexer_2_out, multiplexer_3_out, multiplexer_4_out, multiplexer_6_out, multiplexer_7_out,
       multiplexer_8_out, multiplexer_9_out, PC_q, reg_stage1_1_instrd, reg_stage1_1_pcplus4d,
       reg_stage2_1_signimme, reg_stage2_1_srcae, reg_stage2_1_srcbe, reg_stage3_1_p4, reg_stage3_1_p11,
       reg_stage3_1_p12, reg_stage4_1_aluoutw, reg_stage4_1_readdataw, regfile32_1_rd1, regfile32_1_rd2,
       shifter_2_out;

  Clock clock_1 (.out(CLK));
  Multiplexer #(.width(32)) multiplexer_1 (
    .in0({adder_1_out_2, adder_1_out}), .in1(adder_2_out), .out(multiplexer_1_out), .sel(and_1_out));  // open: en
  Hazard_Unit hazard_unit_1 (
    .BranchD(controlunit_1_out_6), .RegWriteE(reg_stage2_1_regwritee), .RegWriteM(reg_stage3_1_p10),
    .RegWriteW(reg_stage4_1_regwritew), .MemtoRegM(reg_stage3_1_p8), .MemtoRegE(reg_stage2_1_memtorege),
    .WriteRegE(multiplexer_5_out), .RsD(reg_stage1_1_instrd[25:21]), .RsE(reg_stage2_1_rse),
    .RtD(reg_stage1_1_instrd[20:16]), .RtE(reg_stage2_1_rte), .WriteRegM(reg_stage3_1_p13),
    .WriteRegW(reg_stage4_1_writeregw), .StallF(hazard_unit_1_stallf), .StallD(hazard_unit_1_stalld),
    .FlushE(hazard_unit_1_flushe), .ForwardAE(hazard_unit_1_forwardae), .ForwardBE(hazard_unit_1_forwardbe),
    .ForwardAD(hazard_unit_1_forwardad), .ForwardBD(hazard_unit_1_forwardbd), .CLK(CLK));
  Multiplexer #(.width(32)) multiplexer_2 (
    .in0(multiplexer_1_out), .in1({adder_1_out_2, shifter_1_out}), .out(multiplexer_2_out),
    .sel(controlunit_1_out_3));  // open: en
  Register #(.width(32)) PC (.D(multiplexer_2_out), .en(hazard_unit_1_stallf), .Q(PC_q), .clk(CLK));  // open: clr
  Adder #(.width(32)) adder_1 (.a(PC_q), .b(32'h4), .out({adder_1_out_2, adder_1_out}));  // open: cin, cout
  Reg_Stage1 reg_stage1_1 (
    .CLR(and_1_out), .EN(hazard_unit_1_stalld), .CLK(CLK), .InstrF(instmem_1_out_2),
    .PCPlus4F({adder_1_out_2, adder_1_out}), .InstrD(reg_stage1_1_instrd), .PCPlus4D(reg_stage1_1_pcplus4d));
  InstMem instmem_1 (.A(PC_q), .out_2(instmem_1_out_2));
  assign bit_extender_1_out = {{2{reg_stage1_1_instrd[25]}}, reg_stage1_1_instrd[25:0]};  // Bit_Extender bit_extender_1
  ControlUnit controlunit_1 (
    .out_3(controlunit_1_out_3), .in_1(reg_stage1_1_instrd[31:26]), .in_2(reg_stage1_1_instrd[5:0]),
    .out_4(controlunit_1_out_4), .out_5(controlunit_1_out_5), .out_6(controlunit_1_out_6),
    .out_7(controlunit_1_out_7), .out_8(controlunit_1_out_8), .out_9(controlunit_1_out_9),
    .out_10(controlunit_1_out_10));
  Buff_20 buff_20_1 (.in_1(CLK), .out_2(buff_20_1_out_2));
  assign bit_extender_2_out = {{16{reg_stage1_1_instrd[15]}}, reg_stage1_1_instrd[15:0]};  // Bit_Extender bit_extender_2
  Shifter #(.width(28)) shifter_1 (.in(bit_extender_1_out), .\dist (5'b00010), .out(shifter_1_out));
  RegFile32 regfile32_1 (
    .AD1(reg_stage1_1_instrd[25:21]), .AD2(reg_stage1_1_instrd[20:16]), .CLK(buff_20_1_out_2),
    .WE(reg_stage4_1_regwritew), .AD3(reg_stage4_1_writeregw), .WD3(multiplexer_9_out),
    .RD1(regfile32_1_rd1), .RD2(regfile32_1_rd2));
  Shifter #(.width(32)) shifter_2 (.in(bit_extender_2_out), .\dist (5'b00010), .out(shifter_2_out));
  and and_1 (and_1_out, comparator_1_eq, controlunit_1_out_6);
  Comparator #(.width(32)) comparator_1 (
    .a(multiplexer_3_out), .b(multiplexer_4_out), .eq(comparator_1_eq));  // open: gt, lt
  Adder #(.width(32)) adder_2 (.a(shifter_2_out), .b(reg_stage1_1_pcplus4d), .out(adder_2_out));  // open: cin, cout
  Multiplexer #(.width(32)) multiplexer_3 (
    .in0(regfile32_1_rd1), .in1(reg_stage3_1_p11), .out(multiplexer_3_out), .sel(hazard_unit_1_forwardad));  // open: en
  Multiplexer #(.width(32)) multiplexer_4 (
    .in0(regfile32_1_rd2), .in1(reg_stage3_1_p11), .out(multiplexer_4_out), .sel(hazard_unit_1_forwardbd));  // open: en
  Reg_Stage2 reg_stage2_1 (
    .CLK(CLK), .CLR(hazard_unit_1_flushe), .MemtoRegD(controlunit_1_out_4), .MemWriteD(controlunit_1_out_5),
    .ALUSrcD(controlunit_1_out_7), .RegDstD(controlunit_1_out_8), .RegWriteD(controlunit_1_out_9),
    .ALUCtrlD(controlunit_1_out_10), .SrcAD(regfile32_1_rd1), .SrcBD(regfile32_1_rd2),
    .RsD(reg_stage1_1_instrd[25:21]), .RtD(reg_stage1_1_instrd[20:16]), .RdD(reg_stage1_1_instrd[15:11]),
    .SignImmD(bit_extender_2_out), .MemtoRegE(reg_stage2_1_memtorege), .MemWriteE(reg_stage2_1_memwritee),
    .ALUSrcE(reg_stage2_1_alusrce), .RegDstE(reg_stage2_1_regdste), .RegWriteE(reg_stage2_1_regwritee),
    .ALUCtrlE(reg_stage2_1_aluctrle), .SrcAE(reg_stage2_1_srcae), .SrcBE(reg_stage2_1_srcbe),
    .RsE(reg_stage2_1_rse), .RtE(reg_stage2_1_rte), .RdE(reg_stage2_1_rde), .SignImmE(reg_stage2_1_signimme));
  Multiplexer #(.width(5)) multiplexer_5 (
    .in0(reg_stage2_1_rte), .in1(reg_stage2_1_rde), .out(multiplexer_5_out), .sel(reg_stage2_1_regdste));  // open: en
  Multiplexer #(.select(2), .width(32)) multiplexer_6 (
    .in0(reg_stage2_1_srcbe), .in1(reg_stage3_1_p11), .in2(multiplexer_9_out), .out(multiplexer_6_out),
    .sel(hazard_unit_1_forwardbe));  // open: in3, en
  Multiplexer #(.select(2), .width(32)) multiplexer_7 (
    .in0(reg_stage2_1_srcae), .in1(reg_stage3_1_p11), .in2(multiplexer_9_out), .out(multiplexer_7_out),
    .sel(hazard_unit_1_forwardae));  // open: in3, en
  Multiplexer #(.width(32)) multiplexer_8 (
    .in0(multiplexer_6_out), .in1(reg_stage2_1_signimme), .out(multiplexer_8_out), .sel(reg_stage2_1_alusrce));  // open: en
  // Reg_Stage3 reg_stage3_1: pin names not known; wires that end beside it: reg_stage2_1_memtorege, reg_stage2_1_memwritee, reg_stage2_1_regwritee, reg_stage3_1_p4, multiplexer_6_out, multiplexer_5_out, CLK, reg_stage3_1_p8, reg_stage3_1_p9, reg_stage3_1_p10, reg_stage3_1_p11, reg_stage3_1_p12, reg_stage3_1_p13
  ALU alu_1 (
    .SrcA(multiplexer_7_out), .SrcB(multiplexer_8_out), .ALU_Control(reg_stage2_1_aluctrle),
    .ALU_Result(reg_stage3_1_p4));  // open: Zero
  Reg_Stage4 reg_stage4_1 (
    .CLK(CLK), .RegWriteM(reg_stage3_1_p10), .MemtoRegM(reg_stage3_1_p8), .ALUOutM(reg_stage3_1_p11),
    .ReadDataM(datamem_1_rd), .WriteRegM(reg_stage3_1_p13), .RegWriteW(reg_stage4_1_regwritew),
    .MemtoRegW(reg_stage4_1_memtoregw), .ALUOutW(reg_stage4_1_aluoutw), .ReadDataW(reg_stage4_1_readdataw),
    .WriteRegW(reg_stage4_1_writeregw));
  DataMem datamem_1 (.CLK(CLK), .WE(reg_stage3_1_p9), .WD(reg_stage3_1_p12), .A(reg_stage3_1_p11), .RD(datamem_1_rd));
  Multiplexer #(.width(32)) multiplexer_9 (
    .in0(reg_stage4_1_aluoutw), .in1(reg_stage4_1_readdataw), .out(multiplexer_9_out),
    .sel(reg_stage4_1_memtoregw));  // open: en
endmodule

module Buff_20 (
  input  in_1,
  output out_2
);

  wire buffer_1_out, buffer_2_out, buffer_3_out, buffer_4_out, buffer_5_out, buffer_6_out, buffer_7_out,
       buffer_8_out, buffer_9_out, buffer_10_out, buffer_11_out, buffer_12_out, buffer_13_out, buffer_14_out,
       buffer_15_out, buffer_16_out, buffer_17_out, buffer_18_out, buffer_20_out;

  buf buffer_1 (buffer_1_out, in_1);
  buf buffer_2 (buffer_2_out, buffer_1_out);
  buf buffer_3 (buffer_3_out, buffer_5_out);
  buf buffer_4 (buffer_4_out, buffer_2_out);
  buf buffer_5 (buffer_5_out, buffer_6_out);
  buf buffer_6 (buffer_6_out, buffer_4_out);
  buf buffer_7 (buffer_7_out, buffer_8_out);
  buf buffer_8 (buffer_8_out, buffer_9_out);
  buf buffer_9 (buffer_9_out, buffer_10_out);
  buf buffer_10 (buffer_10_out, buffer_3_out);
  buf buffer_11 (buffer_11_out, buffer_7_out);
  buf buffer_12 (buffer_12_out, buffer_13_out);
  buf buffer_13 (buffer_13_out, buffer_11_out);
  buf buffer_14 (buffer_14_out, buffer_12_out);
  buf buffer_15 (buffer_15_out, buffer_17_out);
  buf buffer_16 (buffer_16_out, buffer_18_out);
  buf buffer_17 (buffer_17_out, buffer_14_out);
  buf buffer_18 (buffer_18_out, buffer_15_out);
  buf buffer_19 (out_2, buffer_20_out);
  buf buffer_20 (buffer_20_out, buffer_16_out);
endmodule
